# Fritzing sketch FlashyDelayTrigger (saved by Fritzing 1.0.3b)
breadboards: 1

parts:
  M1 = Arduino Nano (Rev3.0)
  Optocoupler_HCPL-817 = Sharp PC817 [package=THT]
  R5 = Resistor [tolerance=±5% resistance=220 package="2010 [SMD]"]
  R6 = Resistor [tolerance=±5% resistance=220 package="2010 [SMD]"]
  R7 = Resistor [tolerance=±10% resistance=1k package="2010 [SMD]"]
  NPN_1A = TRANSISTOR_NPN_2 [package=to-92]
  LED1 = LED - 5mm [color="White (6500K)" current=0.030A package="5 mm [THT]"]
  X-Sync_OUT = mystery part, 2 pins [chip_label=?]
  X-Sync_In = Pushbutton [package=THT]

nets:
  N1: M1.GND, Optocoupler_HCPL-817.Pin_2, R7.Pin_1, X-Sync_In.leg0
  N2: M1.D2, X-Sync_In.leg1
  N3: M1.D4, R5.Pin_0
  N4: M1.A0, R7.Pin_0, LED1.anode
  N5: M1.3V3, LED1.cathode
  N6: Optocoupler_HCPL-817.Pin_1, R5.Pin_1
  N7: Optocoupler_HCPL-817.Pin_4, NPN_1A.C, X-Sync_OUT.pin1
  N8: Optocoupler_HCPL-817.Pin_3, R6.Pin_1
  N9: R6.Pin_0, NPN_1A.B
  N10: NPN_1A.E, X-Sync_OUT.pin2
