# Fritzing sketch FlashyDelayTrigger (saved by Fritzing 1.0.3b)
breadboards: 1

parts:
  M1 = Arduino Nano (Rev3.0)
  Optocoupler_HCPL-817 = Sharp PC817 [package=THT]
  R5 = Resistor [tolerance=±5% resistance=220 package="2010 [SMD]"]
  R7 = Resistor [tolerance=±10% resistance=1k package="2010 [SMD]"]
  NPN_1A = TRANSISTOR_NPN_2 [package=to-92]
  LED_used_as_Photo-diode = LED - 5mm [color="White (6500K)" current=0.030A package="5 mm [THT]"]
  X-Sync_OUT = mystery part, 2 pins [chip_label=?]
  X-Sync_IN = Pushbutton [package=THT]
  Rotary_Encoder = Rotary Encoder [package=THT]
  Rotary_Switch = Pushbutton [package=THT]
  R8 = Resistor [tolerance=±5% power=0.25W resistance=220 package=THT]
  SSD1306 = SDD1306 [package=THT]

nets:
  GND: M1.GND, Optocoupler_HCPL-817.Pin_2, R7.Pin_1, X-Sync_IN.leg0, Rotary_Encoder.EncoderPinC, Rotary_Switch.leg1, SSD1306.GND
  N1: M1.D2, X-Sync_IN.leg1
  N2: M1.D4, R5.Pin_0
  N3: M1.D7, Rotary_Encoder.EncoderPinA
  N4: M1.D8, Rotary_Encoder.EncoderPinB
  N5: M1.D9, Rotary_Switch.leg0
  5V: M1.5V, SSD1306.VCC
  N6: M1.A5, SSD1306.SCL
  N7: M1.A4, SSD1306.SDA
  N8: M1.A0, R7.Pin_0, LED_used_as_Photo-diode.anode
  N9: M1.3V3, LED_used_as_Photo-diode.cathode
  N10: Optocoupler_HCPL-817.Pin_1, R5.Pin_1
  N11: Optocoupler_HCPL-817.Pin_4, NPN_1A.C, X-Sync_OUT.pin1
  N12: Optocoupler_HCPL-817.Pin_3, R8.Pin_1
  N13: NPN_1A.B, R8.Pin_0
  N14: NPN_1A.E, X-Sync_OUT.pin2

custom parts:
  SDD1306: A standard interface to a SDD1306
